# Fritzing sketch arcade_sketch (saved by Fritzing 0.9.6b)
breadboards: 1
perfboards: 1

parts:
  U1 = attiny85 [package=dip]
  D1 = Schottky Diode [part_number=1N5817 package="300 mil [THT]"]
  D2 = Schottky Diode [part_number=1N5817 package="300 mil [THT]"]
  D3 = Schottky Diode [part_number=1N5817 package="300 mil [THT]"]
  D4 = Schottky Diode [part_number=1N5817 package="300 mil [THT]"]
  R1 = Resistor [tolerance=±5% resistance=220 package="0402 [SMD]"]
  R2 = Resistor [tolerance=±5% resistance=220 package="0402 [SMD]"]
  R3 = Resistor [tolerance=±5% resistance=220 package="0402 [SMD]"]
  R4 = Resistor [tolerance=±5% resistance=220 package="0402 [SMD]"]
  J1 = Camdenboss CTB0158-2 [part_number=CTB0158-2 package=THT]
  CONN1 = USB connector [package=THT]
  S2 = Pushbutton [package="[THT]"]
  S3 = Pushbutton [package="[THT]"]
  S4 = Pushbutton [package="[THT]"]
  S5 = Pushbutton [package="[THT]"]
  LED4 = LED - 3mm [color="Blue (470nm)" current=0.030 package="3 mm [THT]"]
  LED3 = LED - 3mm [color="Yellow (585nm)" package="3 mm [THT]"]
  LED1 = LED - 3mm [color="Red (635nm)" package="3 mm [THT]"]
  LED2 = LED - 3mm [color="Green (560nm)" package="3 mm [THT]"]

nets:
  N1: U1.Pin_2, D1.cathode, LED4.anode
  N2: U1.Pin_3, D2.cathode, LED3.anode
  N3: U1.Pin_4, R1.Pin_1, R2.Pin_1, R3.Pin_1, R4.Pin_1, J1.pin2
  N4: U1.Pin_5, D4.cathode, LED1.anode
  N5: U1.Pin_7, D3.cathode, LED2.anode
  N6: U1.Pin_8, J1.pin1
  N7: D1.anode, S4.Pin_3
  N8: D2.anode, S3.Pin_3, S3.Pin_4
  N9: D3.anode, S5.Pin_1, S5.Pin_2
  N10: D4.anode, S2.Pin_1, S2.Pin_2, S3.Pin_1, S3.Pin_2
  N11: R1.Pin_0, LED2.cathode
  N12: R2.Pin_0, LED3.cathode
  N13: R3.Pin_0, LED4.cathode
  N14: R4.Pin_0, LED1.cathode
  N15: J1.terminal_1, CONN1.GND, CONN1.chassis5, CONN1.chassis6
  N16: J1.terminal_2, CONN1.d-
  N17: S2.Pin_3, S2.Pin_4
