# Fritzing sketch arduino_isp (saved by Fritzing 0.9.6b)
breadboards: 1

parts:
  Part1 = Arduino Uno (Rev3) - ICSP
  U1 = attiny85 [package=dip]
  C1 = Electrolytic Capacitor [capacitance=100μF voltage=35V package="0807 [SMD, electrolytic]"]

nets:
  N1: Part1.ICSP_MISO, Part1.D12/MISO, U1.Pin_6
  N2: Part1.D10_PWM/SS, U1.Pin_1
  N3: Part1.D11_PWM/MOSI, U1.Pin_5
  N4: Part1.D13/SCK, U1.Pin_7
  N5: Part1.RESET, C1.+
  N6: Part1.5V, U1.Pin_8
  N7: Part1.GND, U1.Pin_4, C1.-

notes:
  10uF
